# Fritzing sketch circuit (saved by Fritzing 1.0.1rc)
circuit board: 8.46667cm x 5.64444cm
perfboards: 1

parts:
  Mod1 = Raspberry Pi Pico
  Part1 = Adafruit LM3671 Buck Converter [part_number="Adafruit #2745"]
  Adafruit_CAN_Pal_Breakout1 = Adafruit CAN Pal Breakout [part_number=#5708]
  J1 = screw terminal, 3 pins
  J2 = Screw terminal - 2 pins [package=THT]
  J3 = Screw terminal - 2 pins [package=THT]

nets:
  GND: Mod1.pin_3, Mod1.pin_8, Mod1.pin_13, Mod1.pin_18, Mod1.pin_23, Mod1.pin_28, Mod1.pin_33, Mod1.pin_38, Part1.GND, Adafruit_CAN_Pal_Breakout1.GND, J1.pin2, J3.pin1
  N1: Mod1.pin_21, J1.pin1
  N2: Mod1.pin_31, Adafruit_CAN_Pal_Breakout1.CAN1_TX
  N3: Mod1.pin_32, Adafruit_CAN_Pal_Breakout1.CAN1_RX
  N4: Mod1.pin_36, Adafruit_CAN_Pal_Breakout1.VCC
  N5: Mod1.pin_39, Part1.3.3V, J1.pin3
  N6: Part1.VIN, J3.pin2
  N7: Adafruit_CAN_Pal_Breakout1.CAN_L, J2.pin2
  N8: Adafruit_CAN_Pal_Breakout1.CAN_H, J2.pin1

custom parts:
  Raspberry Pi Pico: Raspberry Pi Pico. Based around the RP2040 microcontroller the Pico is a low cost microcontroller device bringing Raspberry Pi quality, cost, and easy of use to the microcontroller space. Jan 2021, Split part in to two versions: tht (this one) and SMD. This one will drill holes for a .1 in header in pcb to allow plugging in the module as well as providing pads to solder the module to the top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
  Adafruit LM3671 Buck Converter: Your power supply problems just got SUPER SOLVED! This 3.3V Buck Converter Breakout board is great for supplying power to low voltage circuits from a single Li-Ion cell battery or USB power. This chip provides up to 600-mA load current across the entire input voltage range of 3.5 to 5.5V. Great for your portable project, we made this "pin compatible" with the LM1117-3.3V TO-220 chip so you can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
  Adafruit CAN Pal Breakout: If you'd like to connect a board with native CAN Peripheral support, the Adafruit CAN Pal Transceiver will take the 3V logic level signals and convert them to CAN logic levels with the differential signaling required to communicate. Note that not all chips have a CAN peripheral! Some that we know do have it are the ESP32/ESP32-S2/ESP32-S3 (note that ESP32 calls this interface TWAI not CAN)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
